# Fritzing sketch lowpower-sensor-node (saved by Fritzing 0.9.2b)
stripboards: 1

parts:
  U1 = RFM69 [package=rfm69-xxx-s2]
  DHT1 = DHT11 Humitidy and Temperature Sensor
  U2 = atmega328 [package=dip]
  U3 = MCP1702 Voltage Regulator [package="TO92 [THT]"]
  LED1 = LED - 5mm [color="Red (633nm)" package="5 mm [THT]"]
  R2 = Resistor [tolerance=±5% resistance=220 package=THT]
  VCC2 = 4 x AAA Battery Mount
  R3 = Resistor [tolerance=±5% resistance=1M package="2010 [SMD]"]
  R4 = Resistor [tolerance=±5% resistance=1M package="2010 [SMD]"]
  C1 = Ceramic Capacitor [capacitance=10pF package="0603 [SMD, multilayer]"]
  C2 = Ceramic Capacitor [capacitance=10pF package="0603 [SMD, multilayer]"]

nets:
  GND: U1.RESET, U1.DIO0, U1.DIO1, U1.DIO2, U1.DIO3, U1.GND, U1.SCK, U1.MISO, U1.MOSI, U1.NSS, U1.NC, U2.D2, U2.GND, U2.D9_(PWM), U2.D10_(PWM), U2.D11_(PWM), U2.D12, U2.D13, U3.GND, R2.Pin_1, VCC2.-, R3.Pin_1, C1.0, C2.0
  VCC: U1.VCC, DHT1.VDD, U2.VCC, U2.AVCC, U3.Vout, C1.1
  N1: DHT1.DATA, U2.D7
  N2: DHT1.GND, U2.RESET
  N3: U2.D8, LED1.cathode
  N4: U2.A3, R3.Pin_0, R4.Pin_1
  N5: U3.Vin, VCC2.+, R4.Pin_0, C2.1
  N6: LED1.anode, R2.Pin_0

notes:
  Programmed with bootloader for internal clock

custom parts:
  RFM69: The RFM69 is a low-power, low cost radio that is capable of operating in the 434MHz and 900MHz open bands. It's frequency is software defined and there are some very good libraries written for it.
  DHT11 Humitidy and Temperature Sensor: DHT11 Humidity and Temperature Sensor
  MCP1702 Voltage Regulator: A MCP1702 Low Dropout Fixed Voltage Regulator (available in 1.2V, 1.5V, 1.8V, 2.5V, 2.8V, 3.0V, 3.3V, 4.0V, 5.0V)
