# Fritzing sketch sensor-node (saved by Fritzing 0.9.0b)

parts:
  Bauteil1 = Arduino Pro Mini v13
  U1 = RFM69 [package=rfm69-xxx-s2]
  DHT1 = DHT11 Humitidy and Temperature Sensor
  VCC1 = Battery block 9V
  R1 = Resistor [tolerance=±5% resistance=10k package=THT]

nets:
  N1: Bauteil1.RAW, VCC1.+
  GND: Bauteil1.GND, Bauteil1.A2, U1.DIO0, U1.GND, DHT1.GND, VCC1.-
  VCC: Bauteil1.VCC, U1.VCC, DHT1.VDD, R1.Pin_1
  N2: Bauteil1.D13/SCK, U1.SCK
  N3: Bauteil1.D12/MISO, U1.MISO
  N4: Bauteil1.D11_PWM/MOSI, U1.MOSI
  N5: Bauteil1.D10_PWM/SS, U1.NSS
  N6: Bauteil1.D7, DHT1.DATA, R1.Pin_0

custom parts:
  RFM69: The RFM69 is a low-power, low cost radio that is capable of operating in the 434MHz and 900MHz open bands. It's frequency is software defined and there are some very good libraries written for it.
  DHT11 Humitidy and Temperature Sensor: DHT11 Humidity and Temperature Sensor
